# Fritzing sketch led Sketch (saved by Fritzing 0.9.3b)
breadboards: 1

parts:
  Part1 = Arduino Uno (Rev3) - ICSP
  R1 = Resistor [tolerance=±5% resistance=220 package=THT]
  R2 = Resistor [tolerance=±5% resistance=220 package=THT]
  LED1 = LED - 5mm [color="Red (633nm)" package="5 mm [THT]"]
  LED2 = LED - 5mm [color="Blue (525nm)" package="5 mm [THT]"]

nets:
  N1: Part1.D2, R1.Pin_0
  N2: Part1.D4, R2.Pin_0
  N3: Part1.GND, LED1.cathode, LED2.cathode
  N4: R1.Pin_1, LED1.anode
  N5: R2.Pin_1, LED2.anode
