# Fritzing sketch arduino-uno-5-led (saved by Fritzing 0.9.3b)
breadboards: 1

parts:
  LED1 = smd LED [color="Green (570nm)" package="0603 [SMD]"]
  LED2 = smd LED [color="Green (570nm)" package="0603 [SMD]"]
  R2 = Resistor [tolerance=±5% resistance=220 package=THT]
  LED3 = smd LED [color="Green (570nm)" package="0603 [SMD]"]
  LED4 = smd LED [color="Green (570nm)" package="0603 [SMD]"]
  R3 = Resistor [tolerance=±5% resistance=220 package=THT]
  R4 = Resistor [tolerance=±5% resistance=220 package=THT]
  LED5 = smd LED [color="Green (570nm)" package="0603 [SMD]"]
  R5 = Resistor [tolerance=±5% resistance=220 package=THT]
  Part1 = Arduino Uno (Rev3) - ICSP
  R6 = Resistor [tolerance=±5% resistance=220 package=THT]

nets:
  N1: LED1.cathode, R6.Pin_0
  N2: LED1.anode, Part1.D2
  N3: LED2.cathode, R2.Pin_0
  N4: LED2.anode, Part1.D3_PWM
  N5: R2.Pin_1, R3.Pin_1, R4.Pin_1, R5.Pin_1, Part1.GND, R6.Pin_1
  N6: LED3.cathode, R4.Pin_0
  N7: LED3.anode, Part1.D4
  N8: LED4.cathode, R3.Pin_0
  N9: LED4.anode, Part1.D5_PWM
  N10: LED5.cathode, R5.Pin_0
  N11: LED5.anode, Part1.D6_PWM
