# Fritzing sketch esp8266-5-led (saved by Fritzing 0.9.3b)
breadboards: 1

parts:
  U1 = NodeMCU V1.0
  LED1 = smd LED [color="Green (570nm)" package="0603 [SMD]"]
  R1 = Resistor [tolerance=±5% resistance=220 package=THT]
  LED2 = smd LED [color="Green (570nm)" package="0603 [SMD]"]
  R2 = Resistor [tolerance=±5% resistance=220 package=THT]
  LED3 = smd LED [color="Green (570nm)" package="0603 [SMD]"]
  LED4 = smd LED [color="Green (570nm)" package="0603 [SMD]"]
  R3 = Resistor [tolerance=±5% resistance=220 package=THT]
  R4 = Resistor [tolerance=±5% resistance=220 package=THT]
  LED5 = smd LED [color="Green (570nm)" package="0603 [SMD]"]
  R5 = Resistor [tolerance=±5% resistance=220 package=THT]

nets:
  N1: U1.D1, LED1.anode
  N2: U1.D2, LED2.anode
  N3: U1.D3, LED3.anode
  N4: U1.D4, LED4.anode
  N5: U1.GND, R1.Pin_0, R2.Pin_0, R3.Pin_0, R4.Pin_0, R5.Pin_0
  N6: U1.D5, LED5.anode
  N7: LED1.cathode, R1.Pin_1
  N8: LED2.cathode, R2.Pin_1
  N9: LED3.cathode, R4.Pin_1
  N10: LED4.cathode, R3.Pin_1
  N11: LED5.cathode, R5.Pin_1

custom parts:
  NodeMCU V1.0: ESP8266 based NodeMCU
