# Fritzing sketch arduino-l298n-motor-controller (saved by Fritzing 0.9.3b)

parts:
  M1 = DC Motor  # not connected
  M2 = DC Motor  # not connected
  VCC1 = Battery block 9V
  Part1 = Arduino Uno (Rev3) - ICSP

nets:
  N1: VCC1.-, Part1.GND

notes:
  motorB
  motorA
